# Fritzing sketch CIRCUITO_PROTESIS_MIGUELDURAN_FRITZING (saved by Fritzing 0.9.3b)
breadboards: 1

parts:
  part = Arduino Nano (Rev3.0)
  Servo_Giro_Muñeca = Basic Servo
  Servo_Anular_-_Meñique = Basic Servo
  Servo_Indice_-_Medio = Basic Servo
  Sensor_de_Presión = Textile Analog Pressure Sensor [part_number=PW073]
  Bateria_de_6_a_18v = DC Power [voltage=5]
  Regulador_7805 = Voltage Regulator [package=to-220-alt]
  Pot_100K_-_Sensibilidad = POT [package=3362u]
  LED_RGB = RGB LED (com. cathode, rbg) [package="5 mm [THT]"]
  Switch_de_encendido = SWITCH-MOMENTARY-2 [package=tactile-switch-1101ne]

nets:
  N1: part.D2, Servo_Indice_-_Medio.pulse
  N2: part.D3, Servo_Anular_-_Meñique.pulse
  N3: part.D4, Servo_Giro_Muñeca.pulse
  N4: part.D5, LED_RGB.red_anode
  N5: part.D6, LED_RGB.green_anode
  N6: part.D9, LED_RGB.blue_anode
  N7: part.VIN, Regulador_7805.IN, Switch_de_encendido.2
  N8: part.5V, Pot_100K_-_Sensibilidad.S
  N9: part.A3, Sensor_de_Presión.pin_0
  GND: Servo_Giro_Muñeca.gnd, Servo_Anular_-_Meñique.gnd, Servo_Indice_-_Medio.gnd, Bateria_de_6_a_18v.V-, Regulador_7805.GND, LED_RGB.common_cathode
  VCC: Servo_Giro_Muñeca.vcc, Servo_Anular_-_Meñique.vcc, Servo_Indice_-_Medio.vcc, Regulador_7805.OUT
  N10: Sensor_de_Presión.pin_1, Pot_100K_-_Sensibilidad.A
  N11: Bateria_de_6_a_18v.V+, Switch_de_encendido.1
